# Fritzing sketch Potenciometro Arduino (saved by Fritzing 0.9.3b)
breadboards: 1

parts:
  Part1 = Arduino Mega 2560 (Rev3)
  U1 = POT [package=pot_alpha_rv16af-20]

nets:
  N1: Part1.A0, U1.S
  N2: Part1.5V, U1.E
  N3: Part1.GND, U1.A
